# Fritzing sketch Frit_Circuit (saved by Fritzing 0.9.2b)
breadboards: 1

parts:
  Part1 = Arduino Uno (Rev3) - ICSP
  IC1 = L293D [package=THT]
  M2 = DC Motor
  M3 = DC Motor
  J1 = Basic Servo

nets:
  N1: Part1.D9_PWM, J1.pulse
  N2: Part1.D3_PWM, IC1.In_4
  N3: Part1.D4, IC1.In_3
  N4: Part1.D6_PWM, IC1.In_1
  N5: Part1.D7, IC1.In_2
  N6: Part1.5V, IC1.Enable_1, IC1.+Vmotor, IC1.Enable_2, IC1.+V
  N7: IC1.Out_1_(_Controlled_by_Enable_1_), M3.pin_2
  N8: IC1.Out_2_(_Controlled_by_Enable_1_), M3.pin_1
  N9: IC1.Out_3_(_Controlled_by_Enable_2_), M2.pin_2
  N10: IC1.Out_4_(_Controlled_by_Enable_2_), M2.pin_1
